// Logisim project 12_BIT_MISC.circ as structural Verilog: 7 circuits, main circuit ALU
module main (
);

  wire agu_1_ismem, agu_1_istty, alu_1_negative, alu_1_zero, CLOCK_out, control_1_alub, control_1_isblb,
       control_1_isbranchb, control_1_isbranchf, control_1_isj, control_1_issw, control_1_memread,
       control_1_memtoreg, control_1_memwrite, control_1_regwrite, not_1_out, not_2_out;
  wire [1:0] multiplexer_2_out, pccontrol_1_o1;
  wire [2:0] aluop_1_o1;
  wire [6:0] bit_extender_3_out;
  wire [7:0] rom_1_data;
  wire [11:0] adder_1_out, adder_2_out, adder_3_out, adder_4_out, alu_1_out, bit_extender_1_out,
       bit_extender_2_out, multiplexer_1_out, multiplexer_3_out, multiplexer_4_out, negator_1_out, PC_q,
       ram_1_data, regfile_1_aout, regfile_1_bout;
  wire [11:8] rom_1_data_2;

  Register #(.width(12)) PC (.D(multiplexer_1_out), .Q(PC_q), .clk(CLOCK_out));  // open: en, clr
  Adder #(.width(12)) adder_1 (.a(PC_q), .b(12'h1), .out(adder_1_out));  // open: cin, cout
  Multiplexer #(.select(2), .width(12), .enable("false")) multiplexer_1 (
    .in0(adder_1_out), .in1(adder_2_out), .in2(adder_3_out), .in3(adder_4_out), .out(multiplexer_1_out),
    .sel(pccontrol_1_o1));
  ROM #(.addrWidth(12), .dataWidth(12)) rom_1 (.addr(PC_q), .data({rom_1_data_2, rom_1_data}));  // open: sel
  assign bit_extender_1_out = {{4{rom_1_data[7]}}, rom_1_data};  // Bit_Extender bit_extender_1
  Multiplexer #(.width(2), .disabled(0), .enable("false")) multiplexer_2 (
    .in0(rom_1_data[1:0]), .in1(rom_1_data[7:6]), .out(multiplexer_2_out), .sel(control_1_issw));
  assign bit_extender_2_out = {{8{1'b0}}, rom_1_data[3:0]};  // Bit_Extender bit_extender_2
  Negator #(.width(12)) negator_1 (.in(bit_extender_2_out), .out(negator_1_out));
  Adder #(.width(12)) adder_2 (.a(PC_q), .b(bit_extender_1_out), .out(adder_2_out));  // open: cin, cout
  Adder #(.width(12)) adder_3 (.a(PC_q), .b(bit_extender_2_out), .out(adder_3_out));  // open: cin, cout
  Adder #(.width(12)) adder_4 (.a(PC_q), .b(negator_1_out), .out(adder_4_out));  // open: cin, cout
  CONTROL control_1 (
    .A(rom_1_data_2[11]), .B(rom_1_data_2[10]), .C(rom_1_data_2[9]), .D(rom_1_data_2[8]),
    .RegWrite(control_1_regwrite), .ALUB(control_1_alub), .MemToReg(control_1_memtoreg),
    .MemWrite(control_1_memwrite), .MemRead(control_1_memread), .IsBranchF(control_1_isbranchf),
    .IsBranchB(control_1_isbranchb), .IsJ(control_1_isj), .IsBLB(control_1_isblb), .IsSw(control_1_issw));  // open: IsSubIMM
  ALUOP aluop_1 (
    .A(rom_1_data_2[11]), .B(rom_1_data_2[10]), .C(rom_1_data_2[9]), .D(rom_1_data_2[8]), .O3(aluop_1_o1[2]),
    .O2(aluop_1_o1[1]), .O1(aluop_1_o1[0]));
  REGFILE regfile_1 (
    .A(rom_1_data[5:4]), .B(multiplexer_2_out), .RWRITE(rom_1_data[7:6]), .DATA(multiplexer_4_out),
    .AOUT(regfile_1_aout), .BOUT(regfile_1_bout), .WRITE(control_1_regwrite), .CLOCK(not_1_out));
  not not_1 (not_1_out, CLOCK_out);
  PCCONTROL pccontrol_1 (
    .ZeroFlag(alu_1_zero), .NegativeFlag(alu_1_negative), .IsBranchF(control_1_isbranchf),
    .IsBranchB(control_1_isbranchb), .IsJ(control_1_isj), .IsBLB(control_1_isblb), .O2(pccontrol_1_o1[1]),
    .O1(pccontrol_1_o1[0]));
  Multiplexer #(.width(12), .disabled(0), .enable("false")) multiplexer_3 (
    .in0(regfile_1_bout), .in1(bit_extender_2_out), .out(multiplexer_3_out), .sel(control_1_alub));
  ALU alu_1 (
    .A(regfile_1_aout), .B(multiplexer_3_out), .OUT(alu_1_out), .SELECT(aluop_1_o1), .ZERO(alu_1_zero),
    .NEGATIVE(alu_1_negative));
  Multiplexer #(.width(12), .disabled(0), .enable("false")) multiplexer_4 (
    .in0(alu_1_out), .in1(ram_1_data), .out(multiplexer_4_out), .sel(control_1_memtoreg));
  Bit_Extender #(.in_width(12), .out_width(7)) bit_extender_3 (.in(regfile_1_bout), .out(bit_extender_3_out));
  AGU agu_1 (.ADDRESS(alu_1_out), .IsMem(agu_1_ismem), .IsTTY(agu_1_istty), .IsSW(control_1_memwrite));
  TTY tty_1 (.data(bit_extender_3_out), .clk(not_2_out), .we(agu_1_istty));  // open: clr
  RAM #(.addrWidth(12), .dataWidth(12), .bus("separate")) ram_1 (
    .addr(alu_1_out), .din(regfile_1_bout), .data(ram_1_data), .str(control_1_memwrite), .sel(agu_1_ismem),
    .clk(not_2_out), .ld(control_1_memread));  // open: clr
  not not_2 (not_2_out, CLOCK_out);
  Clock CLOCK (.out(CLOCK_out));

  // Notes on the sheet:
  //   INSTRUCTION MEMORY
  //   contents of rom_1 (hex, n*v repeats v):
  //   0 2f8 209 0 0 0 930 100 208 0 0 0 205 931 100 209 0 0 0 204 932 933 100 20a 0 0 0 301 934 100 20f 0
  //   203 935 100 20a 936 830 910 831 910 832 910 833 910 834 910 835 910 836 910 100 cf1
  //   JUMP
  //   BF
  //   BB
  //   DATA MEMORY
  //   ADD
  //   SUB
  //   ADDI
  //   SUBI
  //   AND
  //   OR
  //   XOR
  //   NOR
  //   LW
  //   SW
  //   SRL
  //   SRA
  //   JUMP
  //   BEQF
  //   BEQB
  //   BLB
  //   12 BIT INSTRUCTION WORD - 4 BIT OPCODE
endmodule

module ALU (
  input  [2:0] SELECT,
  input  [11:0] A,
  input  [11:0] B,
  output NEGATIVE,
  output ZERO,
  output [11:0] OUT
);

  wire [11:0] adder_1_out, and_1_out, nor_1_out, or_1_out, shifter_1_out, shifter_2_out, subtractor_1_out,
       xor_1_out;

  Adder #(.width(12)) adder_1 (.a(A), .b(B), .out(adder_1_out));  // open: cin, cout
  Subtractor #(.width(12)) subtractor_1 (.a(A), .b(B), .out(subtractor_1_out));  // open: bin, bout
  assign and_1_out = A & B;  // AND_Gate and_1, 12 bits wide
  assign or_1_out = A | B;  // OR_Gate or_1, 12 bits wide
  assign xor_1_out = A ^ B;  // XOR_Gate xor_1, 12 bits wide
  assign nor_1_out = ~(A | B);  // NOR_Gate nor_1, 12 bits wide
  Shifter #(.width(12), .shift("ar")) shifter_1 (.in(A), .\dist (4'b0001), .out(shifter_1_out));
  Shifter #(.width(12), .shift("lr")) shifter_2 (.in(A), .\dist (4'b0001), .out(shifter_2_out));
  Multiplexer #(.select(3), .width(12), .disabled(0), .enable("false")) multiplexer_1 (
    .in0(adder_1_out), .in1(subtractor_1_out), .in2(and_1_out), .in3(or_1_out), .in4(xor_1_out),
    .in5(nor_1_out), .in6(shifter_1_out), .in7(shifter_2_out), .out({NEGATIVE, OUT[10:0]}), .sel(SELECT));
  nor nor_2 (ZERO, NEGATIVE, OUT[10], OUT[9], OUT[8], OUT[7], OUT[6], OUT[5], OUT[4], OUT[3], OUT[2], OUT[1], OUT[0]);

  assign OUT[11] = NEGATIVE;
endmodule

// REG
module REGFILE (
  input  WRITE,
  input  CLOCK,
  input  [1:0] A,
  input  [1:0] B,
  input  [1:0] RWRITE,
  input  [11:0] DATA,
  output [11:0] AOUT,
  output [11:0] BOUT
);

  wire demultiplexer_1_out0, demultiplexer_1_out1, demultiplexer_1_out2, demultiplexer_1_out3;
  wire [11:0] register_1_q, register_2_q, register_3_q, register_4_q;

  Demultiplexer #(.select(2), .disabled(0), .enable("false")) demultiplexer_1 (
    .out0(demultiplexer_1_out0), .out1(demultiplexer_1_out1), .out2(demultiplexer_1_out2),
    .out3(demultiplexer_1_out3), .in(WRITE), .sel(RWRITE));
  Register #(.width(12)) register_1 (.D(DATA), .en(demultiplexer_1_out0), .Q(register_1_q), .clk(CLOCK));  // open: clr
  Register #(.width(12)) register_2 (.D(DATA), .en(demultiplexer_1_out1), .Q(register_2_q), .clk(CLOCK));  // open: clr
  Register #(.width(12)) register_3 (.D(DATA), .en(demultiplexer_1_out2), .Q(register_3_q), .clk(CLOCK));  // open: clr
  Register #(.width(12)) register_4 (.D(DATA), .en(demultiplexer_1_out3), .Q(register_4_q), .clk(CLOCK));  // open: clr
  Multiplexer #(.select(2), .width(12), .disabled(0), .enable("false")) multiplexer_1 (
    .in0(register_1_q), .in1(register_2_q), .in2(register_3_q), .in3(register_4_q), .out(AOUT), .sel(A));
  Multiplexer #(.select(2), .width(12), .disabled(0), .enable("false")) multiplexer_2 (
    .in0(register_1_q), .in1(register_2_q), .in2(register_3_q), .in3(register_4_q), .out(BOUT), .sel(B));
endmodule

module PCCONTROL (
  input  ZeroFlag,
  input  NegativeFlag,
  input  IsBranchF,
  input  IsBranchB,
  input  IsJ,
  input  IsBLB,
  output O2,
  output O1
);

  wire and_1_out, and_2_out, and_3_out, and_4_out, and_5_out, and_6_out, and_7_out, not_1_out, not_2_out,
       not_3_out, not_4_out, not_5_out, not_6_out, not_7_out, not_8_out, not_9_out, not_10_out, not_11_out,
       not_12_out, not_13_out, not_14_out, not_15_out, not_16_out, not_17_out, not_18_out, not_19_out,
       not_20_out, not_21_out, not_22_out, not_23_out, not_24_out, not_25_out, not_26_out, not_27_out,
       not_28_out;

  not not_1 (not_1_out, ZeroFlag);
  not not_2 (not_2_out, IsBranchF);
  not not_3 (not_3_out, IsBranchB);
  not not_4 (not_4_out, IsJ);
  not not_5 (not_5_out, NegativeFlag);
  not not_6 (not_6_out, IsBranchF);
  not not_7 (not_7_out, IsJ);
  not not_8 (not_8_out, IsBLB);
  not not_9 (not_9_out, NegativeFlag);
  not not_10 (not_10_out, IsBranchB);
  not not_11 (not_11_out, IsJ);
  not not_12 (not_12_out, IsBLB);
  not not_13 (not_13_out, ZeroFlag);
  not not_14 (not_14_out, IsBranchF);
  not not_15 (not_15_out, IsBranchB);
  not not_16 (not_16_out, IsBLB);
  not not_17 (not_17_out, NegativeFlag);
  not not_18 (not_18_out, IsBranchF);
  not not_19 (not_19_out, IsBranchB);
  not not_20 (not_20_out, IsBLB);
  not not_21 (not_21_out, ZeroFlag);
  not not_22 (not_22_out, IsBranchF);
  not not_23 (not_23_out, IsBranchB);
  not not_24 (not_24_out, IsJ);
  not not_25 (not_25_out, NegativeFlag);
  not not_26 (not_26_out, IsBranchF);
  not not_27 (not_27_out, IsJ);
  not not_28 (not_28_out, IsBLB);
  and and_1 (and_1_out, not_1_out, NegativeFlag, not_2_out, not_3_out, not_4_out, IsBLB);
  and and_2 (and_2_out, ZeroFlag, not_5_out, not_6_out, IsBranchB, not_7_out, not_8_out);
  and and_3 (and_3_out, ZeroFlag, not_9_out, IsBranchF, not_10_out, not_11_out, not_12_out);
  and and_4 (and_4_out, not_13_out, not_14_out, not_15_out, IsJ, not_16_out);
  and and_5 (and_5_out, not_17_out, not_18_out, not_19_out, IsJ, not_20_out);
  and and_6 (and_6_out, not_21_out, NegativeFlag, not_22_out, not_23_out, not_24_out, IsBLB);
  and and_7 (and_7_out, ZeroFlag, not_25_out, not_26_out, IsBranchB, not_27_out, not_28_out);
  or or_1 (O2, and_1_out, and_2_out, and_3_out);
  or or_2 (O1, and_4_out, and_5_out, and_6_out, and_7_out);
endmodule

module ALUOP (
  input  A,
  input  B,
  input  C,
  input  D,
  output O3,
  output O2,
  output O1
);

  wire and_1_out, and_2_out, and_3_out, and_4_out, and_5_out, and_6_out, and_7_out, and_8_out, not_1_out,
       not_2_out, not_3_out, not_4_out, not_5_out, not_6_out;

  not not_1 (not_1_out, A);
  and and_1 (and_1_out, not_1_out, B, C);
  and and_2 (and_2_out, A, not_2_out, C);
  not not_2 (not_2_out, B);
  not not_3 (not_3_out, A);
  and and_3 (and_3_out, not_3_out, B, not_4_out);
  not not_4 (not_4_out, C);
  and and_4 (and_4_out, A, not_5_out, C);
  not not_5 (not_5_out, B);
  not not_6 (not_6_out, A);
  and and_5 (and_5_out, not_6_out, D);
  and and_6 (and_6_out, C, D);
  and and_7 (and_7_out, B, D);
  and and_8 (and_8_out, A, B, C);
  or or_1 (O3, and_1_out, and_2_out);
  or or_2 (O2, and_3_out, and_4_out);
  or or_3 (O1, and_5_out, and_6_out, and_7_out, and_8_out);
endmodule

module CONTROL (
  input  A,
  input  B,
  input  C,
  input  D,
  output RegWrite,
  output ALUB,
  output MemToReg,
  output MemWrite,
  output MemRead,
  output IsBranchF,
  output IsBranchB,
  output IsJ,
  output IsBLB,
  output IsSw,
  output IsSubIMM
);

  wire and_1_out, and_2_out, and_3_out, and_4_out, and_13_out, not_1_out, not_2_out, not_3_out, not_4_out,
       not_5_out, not_6_out, not_7_out, not_8_out, not_9_out, not_10_out, not_11_out, not_12_out, not_13_out,
       not_14_out, not_15_out, not_16_out, not_17_out, not_18_out, not_19_out, not_20_out, not_21_out,
       not_22_out;

  not not_1 (not_1_out, A);
  not not_2 (not_2_out, B);
  and and_1 (and_1_out, not_2_out, not_3_out);
  not not_3 (not_3_out, D);
  not not_4 (not_4_out, B);
  and and_2 (and_2_out, not_4_out, C);
  not not_5 (not_5_out, A);
  not not_6 (not_6_out, B);
  and and_3 (and_3_out, not_5_out, not_6_out, C);
  and and_4 (and_4_out, A, not_7_out, not_8_out);
  not not_7 (not_7_out, B);
  not not_8 (not_8_out, C);
  not not_9 (not_9_out, B);
  not not_10 (not_10_out, C);
  not not_11 (not_11_out, D);
  not not_12 (not_12_out, B);
  not not_13 (not_13_out, C);
  not not_14 (not_14_out, B);
  not not_15 (not_15_out, C);
  not not_16 (not_16_out, D);
  not not_17 (not_17_out, C);
  not not_18 (not_18_out, D);
  not not_19 (not_19_out, C);
  not not_20 (not_20_out, D);
  and and_5 (IsBLB, A, B, C, D);
  not not_21 (not_21_out, B);
  not not_22 (not_22_out, C);
  and and_6 (IsSubIMM, D, C, ~B, ~A);  // AND_Gate
  or or_1 (RegWrite, not_1_out, and_1_out, and_2_out);
  or or_2 (ALUB, and_3_out, and_4_out);
  and and_7 (MemToReg, A, not_9_out, not_10_out, not_11_out);
  and and_8 (MemWrite, A, not_12_out, not_13_out, D);
  and and_9 (MemRead, A, not_14_out, not_15_out, not_16_out);
  and and_10 (IsBranchF, A, B, not_17_out, D);
  and and_11 (IsBranchB, A, B, C, not_18_out);
  and and_12 (IsJ, A, B, not_19_out, not_20_out);
  or or_3 (IsSw, IsBranchB, IsBranchF, and_13_out);
  and and_13 (and_13_out, A, not_21_out, not_22_out, D);
endmodule

module AGU (
  input  [11:0] ADDRESS,
  input  IsSW,
  output IsMem,
  output IsTTY
);

  wire nor_1_out;

  nor nor_1 (nor_1_out, ADDRESS[0], ADDRESS[1], ADDRESS[2], ADDRESS[3], ADDRESS[4], ADDRESS[5], ADDRESS[6], ADDRESS[7], ADDRESS[8], ADDRESS[9], ADDRESS[10], ADDRESS[11]);
  not not_1 (IsMem, nor_1_out);
  and and_1 (IsTTY, nor_1_out, IsSW);
endmodule
